// Logisim project Processor.circ as structural Verilog: 5 circuits, main circuit main
module main (
);

  wire alu_1_out_5, clock_1_out, clock_2_out, clock_3_out, undriven_6, undriven_8;
  wire [3:0] icode, ifun, rA_q, rB_q, undriven, undriven_2, undriven_3, undriven_4, undriven_9;
  wire [7:0] alu_1_out_4, register_file_1_out_8, register_file_1_out_9, undriven_5, undriven_7, val_A_q,
       val_B_q, val_C_q, val_E_q;

  Register #(.width(4)) u_icode (.D(undriven), .Q(icode), .clk(clock_1_out));  // open: en, clr
  Register #(.width(4)) u_ifun (.D(undriven_2), .Q(ifun), .clk(clock_1_out));  // open: en, clr
  Register #(.width(4)) rA (.D(undriven_3), .Q(rA_q), .clk(clock_1_out));  // open: en, clr
  Memory memory_1 ();  // open: Address_Bus, in_2, in_3, Data_Bus
  Register #(.width(4)) rB (.D(undriven_4), .Q(rB_q), .clk(clock_1_out));  // open: en, clr
  Register val_C (.D(undriven_5), .Q(val_C_q), .clk(clock_1_out));  // open: en, clr
  Clock clock_1 (.out(clock_1_out));
  ALU alu_1 (.out_4(alu_1_out_4), .out_5(alu_1_out_5), .in_1(ifun[1:0]));  // open: in_2, in_3
  Register val_E (.D(alu_1_out_4), .en(icode[3]), .Q(val_E_q), .clk(clock_2_out));  // open: clr
  Clock clock_2 (.out(clock_2_out));
  Register val_A (.D(register_file_1_out_8), .en(undriven_6), .Q(val_A_q), .clk(clock_3_out));  // open: clr
  Register_File register_file_1 (
    .in_5(undriven_7), .in_6(undriven_8), .in_7(undriven_9), .out_8(register_file_1_out_8),
    .in_1(undriven_6), .in_2(rA_q), .out_9(register_file_1_out_9), .in_3(undriven_6), .in_4(rB_q));
  Register val_B (.D(register_file_1_out_9), .en(undriven_6), .Q(val_B_q), .clk(clock_3_out));  // open: clr
  Clock clock_3 (.out(clock_3_out));
endmodule

module ALU (
  input  [1:0] in_1,
  input  [7:0] in_2,
  input  [7:0] in_3,
  output [7:0] out_4,
  output out_5
);

  wire clock_1_out, nor_1_out;
  wire [7:0] adder_1_out, multiplier_1_out;

  nor nor_1 (nor_1_out, out_4[0], out_4[1], out_4[2], out_4[3], out_4[4], out_4[5], out_4[6], out_4[7]);
  Register #(.width(1)) ZF (.D(nor_1_out), .en(in_1[0]), .Q(out_5), .clk(clock_1_out));  // open: clr
  Clock clock_1 (.out(clock_1_out));
  Multiplexer #(.width(8), .disabled(0), .enable("false")) multiplexer_1 (
    .in0(adder_1_out), .in1(multiplier_1_out), .out(out_4), .sel(in_1[1]));
  Adder adder_1 (.a(in_2), .b(in_3), .out(adder_1_out));  // open: cin, cout
  Multiplier multiplier_1 (.a(in_2), .b(in_3), .out(multiplier_1_out));  // open: cin, cout

  // Notes on the sheet:
  //   bit 0: 0 = add, 1 = multiply
  //   bit 1: 0 = don't update ZF, 1 = update ZF
endmodule

module Register_File (
  input  in_1,
  input  [3:0] in_2,
  input  in_3,
  input  [3:0] in_4,
  input  [7:0] in_5,
  input  in_6,
  input  [3:0] in_7,
  output [7:0] out_8,
  output [7:0] out_9
);

  wire clock_1_out;
  wire [7:0] A_q, B_q, C_q, D_q, demultiplexer_2_out0, demultiplexer_2_out1, demultiplexer_2_out2,
       demultiplexer_2_out3, demultiplexer_2_out4, demultiplexer_2_out5, demultiplexer_2_out6,
       demultiplexer_2_out7, demultiplexer_2_out8, demultiplexer_2_out9, demultiplexer_2_out10,
       demultiplexer_2_out11, demultiplexer_2_out12, demultiplexer_2_out13, demultiplexer_2_out14,
       demultiplexer_2_out15, E_q, F_q, G_q, H_q, I_q, J_q, K_q, L_q, M_q, N_q, rbp_q, rsp_q;
  wire [15:0] demultiplexer_1_out0;

  Demultiplexer #(.select(4), .enable("false")) demultiplexer_1 (
    .out0(demultiplexer_1_out0[0]), .out1(demultiplexer_1_out0[1]), .out2(demultiplexer_1_out0[2]),
    .out3(demultiplexer_1_out0[3]), .out4(demultiplexer_1_out0[4]), .out5(demultiplexer_1_out0[5]),
    .out6(demultiplexer_1_out0[6]), .out7(demultiplexer_1_out0[7]), .out8(demultiplexer_1_out0[8]),
    .out9(demultiplexer_1_out0[9]), .out10(demultiplexer_1_out0[10]), .out11(demultiplexer_1_out0[11]),
    .out12(demultiplexer_1_out0[12]), .out13(demultiplexer_1_out0[13]), .out14(demultiplexer_1_out0[14]),
    .out15(demultiplexer_1_out0[15]), .in(in_6), .sel(in_7));
  Demultiplexer #(.select(4), .width(8), .disabled(0)) demultiplexer_2 (
    .out0(demultiplexer_2_out0), .out1(demultiplexer_2_out1), .out2(demultiplexer_2_out2),
    .out3(demultiplexer_2_out3), .out4(demultiplexer_2_out4), .out5(demultiplexer_2_out5),
    .out6(demultiplexer_2_out6), .out7(demultiplexer_2_out7), .out8(demultiplexer_2_out8),
    .out9(demultiplexer_2_out9), .out10(demultiplexer_2_out10), .out11(demultiplexer_2_out11),
    .out12(demultiplexer_2_out12), .out13(demultiplexer_2_out13), .out14(demultiplexer_2_out14),
    .out15(demultiplexer_2_out15), .in(in_5), .sel(in_7), .en(in_6));
  Clock clock_1 (.out(clock_1_out));
  Register A (.D(demultiplexer_2_out0), .en(demultiplexer_1_out0[0]), .Q(A_q), .clk(clock_1_out));  // open: clr
  Register B (.D(demultiplexer_2_out1), .en(demultiplexer_1_out0[1]), .Q(B_q), .clk(clock_1_out));  // open: clr
  Register C (.D(demultiplexer_2_out2), .en(demultiplexer_1_out0[2]), .Q(C_q), .clk(clock_1_out));  // open: clr
  Register D (.D(demultiplexer_2_out3), .en(demultiplexer_1_out0[3]), .Q(D_q), .clk(clock_1_out));  // open: clr
  Register E (.D(demultiplexer_2_out4), .en(demultiplexer_1_out0[4]), .Q(E_q), .clk(clock_1_out));  // open: clr
  Register F (.D(demultiplexer_2_out5), .en(demultiplexer_1_out0[5]), .Q(F_q), .clk(clock_1_out));  // open: clr
  Register G (.D(demultiplexer_2_out6), .en(demultiplexer_1_out0[6]), .Q(G_q), .clk(clock_1_out));  // open: clr
  Register H (.D(demultiplexer_2_out7), .en(demultiplexer_1_out0[7]), .Q(H_q), .clk(clock_1_out));  // open: clr
  Register I (.D(demultiplexer_2_out8), .en(demultiplexer_1_out0[8]), .Q(I_q), .clk(clock_1_out));  // open: clr
  Register J (.D(demultiplexer_2_out9), .en(demultiplexer_1_out0[9]), .Q(J_q), .clk(clock_1_out));  // open: clr
  Register K (.D(demultiplexer_2_out10), .en(demultiplexer_1_out0[10]), .Q(K_q), .clk(clock_1_out));  // open: clr
  Register L (.D(demultiplexer_2_out11), .en(demultiplexer_1_out0[11]), .Q(L_q), .clk(clock_1_out));  // open: clr
  Register M (.D(demultiplexer_2_out12), .en(demultiplexer_1_out0[12]), .Q(M_q), .clk(clock_1_out));  // open: clr
  Register N (.D(demultiplexer_2_out13), .en(demultiplexer_1_out0[13]), .Q(N_q), .clk(clock_1_out));  // open: clr
  Register rbp (.D(demultiplexer_2_out14), .en(demultiplexer_1_out0[14]), .Q(rbp_q), .clk(clock_1_out));  // open: clr
  Register rsp (.D(demultiplexer_2_out15), .en(demultiplexer_1_out0[15]), .Q(rsp_q), .clk(clock_1_out));  // open: clr
  Multiplexer #(.select(4), .width(8), .disabled(0)) multiplexer_1 (
    .in0(A_q), .in1(B_q), .in2(C_q), .in3(D_q), .in4(E_q), .in5(F_q), .in6(G_q), .in7(H_q), .in8(I_q),
    .in9(J_q), .in10(K_q), .in11(L_q), .in12(M_q), .in13(N_q), .in14(rbp_q), .in15(rsp_q), .out(out_8),
    .sel(in_2), .en(in_1));
  Multiplexer #(.select(4), .width(8), .disabled(0)) multiplexer_2 (
    .in0(A_q), .in1(B_q), .in2(C_q), .in3(D_q), .in4(E_q), .in5(F_q), .in6(G_q), .in7(H_q), .in8(I_q),
    .in9(J_q), .in10(K_q), .in11(L_q), .in12(M_q), .in13(N_q), .in14(rbp_q), .in15(rsp_q), .out(out_9),
    .sel(in_4), .en(in_3));
endmodule

module Memory (
  input  [7:0] Address_Bus,
  input  [7:0] in_2,
  input  [1:0] in_3,
  output [7:0] Data_Bus
);

  wire _01_out, _10_out, clock_1_out, sel_out;
  wire [7:0] ram_1_data, register_1_q;

  Register register_1 (.D(Address_Bus), .Q(register_1_q), .clk(clock_1_out));  // open: en, clr
  and _01 (_01_out, ~in_3[0], in_3[1]);  // AND_Gate
  and _10 (_10_out, in_3[0], ~in_3[1]);  // AND_Gate
  xor sel (sel_out, in_3[0], in_3[1]);
  Clock clock_1 (.out(clock_1_out));
  RAM #(.bus("separate")) ram_1 (
    .addr(register_1_q), .din(in_2), .data(ram_1_data), .str(_01_out), .sel(sel_out), .clk(clock_1_out),
    .ld(_10_out));  // open: clr
  Register register_2 (.D(ram_1_data), .Q(Data_Bus), .clk(clock_1_out));  // open: en, clr

  // Notes on the sheet:
  //   00 - Do Nothing
  //   01 - Read
  //   10 - Write
  //   Data_in
  //   RAM
  //   store_data_en
  //   load_data_en
  //   ROM
  //   ROM_select_en
endmodule

module Write_Back (
  input  [7:0] in_1,
  input  [7:0] in_2,
  input  [7:0] in_3,
  input  [3:0] icode,
  input  cnd,
  output [7:0] out_6
);

  wire _0001_out, _0010_out, _0011_out, _0100_out, _0111_2_out, _0111_out, _1000_out, _1101_out, _1110_out,
       _1111_out;
  wire [1:0] or_1_out;

  and _0100 (_0100_out, ~icode[0], ~icode[1], icode[2], ~icode[3]);  // AND_Gate
  and _0011 (_0011_out, icode[0], icode[1], ~icode[2], ~icode[3]);  // AND_Gate
  or or_1 (or_1_out[0], _0100_out, _0011_out, _1101_out, _1110_out, _1000_out, _1111_out, _0111_out, _0111_2_out, _0010_out);
  and _1101 (_1101_out, icode[0], ~icode[1], icode[2], icode[3]);  // AND_Gate
  and _1110 (_1110_out, ~icode[0], icode[1], icode[2], icode[3]);  // AND_Gate
  and _1000 (_1000_out, ~icode[0], ~icode[1], ~icode[2]);  // AND_Gate
  and _1111 (_1111_out, icode[0], icode[1], icode[2], icode[3]);
  Multiplexer #(.select(2), .width(8)) multiplexer_1 (
    .in1(in_1), .in2(in_2), .in3(in_3), .out(out_6), .sel(or_1_out));  // open: in0, en
  and _0111 (_0111_out, icode[0], icode[1], ~cnd, icode[2], ~icode[3]);  // AND_Gate
  or or_2 (or_1_out[1], _0111_2_out, _0010_out, _0001_out);
  and _0010 (_0010_out, ~icode[0], icode[1], ~icode[2], ~icode[3]);  // AND_Gate
  and _0111_2 (_0111_2_out, icode[0], icode[1], cnd, icode[2], ~icode[3]);  // AND_Gate
  and _0001 (_0001_out, icode[0], ~icode[1], ~icode[2], ~icode[3]);  // AND_Gate

  // Notes on the sheet:
  //   INPUTS
  //   01 ValP
  //   10 ValM
  //   11 ValC
  //   icode:
  //   irmov - 11
  //   rrmovl - 100
  //   ld - 1101
  //   st -1110
  //   jmp - 111
  //   halt - 0
  //   add - 1111
  //   mul - 1000
  //   call - 10
  //   return - 1
  //   PC <- valP
  //   PC <- valP
  //   PC <- valP
  //   PC <- valP
  //   PC <- valP
  //   PC <- valP
  //   PC <- valC
  //   PC <- valM
  //   PC <- cond ? valC : val P
  //   10 valM = 0001
  //   11 valC = 0010 + 0111*cnd
  //   01 valP = 0011 + 0100 + 1101 + 1110 + 0111*cnd' + 1111 + 1000 
endmodule
